// Logisim project BENSALEM_ADEM_10.circ as structural Verilog: 10 circuits, main circuit INTERRUPT HIERARCHY
// INNTERRUPT HIERARCHY
module INTERRUPT_HIERARCHY (
  input  POWER_FAILURES,
  input  DISK_0,
  input  DISK_1,
  input  DISK_2,
  input  DISK_3,
  input  [5:0] ALARM,
  input  [3:0] RES,
  output INT_L1_0,
  output INT_L1_1,
  output INT_L1_2,
  output INT_L1_3,
  output [1:0] LEVEL_Number
);

  wire and_1_out, and_6_out, and_7_out, and_8_out, and_9_out, and_10_out, and_11_out, and_12_out, and_13_out,
       and_14_out, and_15_out, and_16_out, and_17_out, and_18_out, and_19_out, and_20_out, CLK, d_ff_1_q,
       d_ff_2_q, d_ff_3_q, d_ff_4_q, d_ff_5_q, d_ff_6_q, d_ff_7_q, d_ff_8_q, d_ff_9_q, d_ff_10_q, d_ff_11_q,
       d_ff_16_q, d_ff_17_q, d_ff_18_q, d_ff_19_q, d_ff_20_q, d_ff_21_q, d_ff_22_q, d_ff_23_q, d_ff_24_q,
       d_ff_25_q, d_ff_26_q, d_ff_27_q, d_ff_28_q, d_ff_29_q, d_ff_30_q, d_ff_31_q, d_ff_32_q, d_ff_33_q,
       d_ff_34_q, d_ff_35_q, d_ff_36_q, d_ff_37_q, d_ff_38_q, d_ff_39_q, d_ff_40_q, LEVEL0, LEVEL1, LEVEL2,
       LEVEL3, or_1_out, or_2_out, or_3_out, or_4_out, undriven;

  Clock clock_1 (.out(CLK));
  D_Flip_Flop #(.trigger("high")) d_ff_1 (.clk(CLK), .D(LEVEL0), .Q(d_ff_1_q));  // open: Qn, preset, en, reset
  D_Flip_Flop #(.trigger("high")) d_ff_2 (.clk(CLK), .D(LEVEL1), .Q(d_ff_2_q));  // open: Qn, preset, en, reset
  D_Flip_Flop #(.trigger("high")) d_ff_3 (.clk(CLK), .D(LEVEL2), .Q(d_ff_3_q));  // open: Qn, preset, en, reset
  D_Flip_Flop #(.trigger("high")) d_ff_4 (.clk(CLK), .D(LEVEL3), .Q(d_ff_4_q));  // open: Qn, preset, en, reset
  D_Flip_Flop #(.trigger("high")) d_ff_5 (.clk(CLK), .D(1'b1), .Q(d_ff_5_q));  // open: Qn, preset, en, reset
  // Probe on d_ff_6_q
  D_Flip_Flop #(.trigger("high")) d_ff_6 (.clk(CLK), .D(and_1_out), .Q(d_ff_6_q));  // open: Qn, preset, en, reset
  or or_1 (or_1_out, d_ff_4_q, d_ff_3_q, d_ff_2_q, d_ff_1_q);
  and and_1 (and_1_out, d_ff_5_q, or_1_out);
  and and_2 (LEVEL0, d_ff_11_q, d_ff_7_q);
  and and_3 (LEVEL1, or_2_out, d_ff_8_q);
  and and_4 (LEVEL2, or_3_out, d_ff_9_q);
  and and_5 (LEVEL3, or_4_out, d_ff_10_q);
  D_Flip_Flop #(.trigger("high")) d_ff_7 (.clk(CLK), .D(1'b1), .Q(d_ff_7_q));  // open: Qn, preset, en, reset
  D_Flip_Flop #(.trigger("high")) d_ff_8 (.clk(CLK), .D(1'b1), .Q(d_ff_8_q));  // open: Qn, preset, en, reset
  D_Flip_Flop #(.trigger("high")) d_ff_9 (.clk(CLK), .D(1'b1), .Q(d_ff_9_q));  // open: Qn, preset, en, reset
  D_Flip_Flop #(.trigger("high")) d_ff_10 (.clk(CLK), .D(1'b1), .Q(d_ff_10_q));  // open: Qn, preset, en, reset
  or or_2 (or_2_out, INT_L1_0, INT_L1_1, INT_L1_2, INT_L1_3);
  or or_3 (or_3_out, d_ff_17_q, d_ff_18_q, d_ff_19_q, d_ff_20_q, d_ff_21_q, d_ff_22_q);
  PRIORITY_ENCODER priority_encoder_1 (
    .L0(LEVEL0), .L1(LEVEL1), .L2(LEVEL2), .L3(LEVEL3), .Device_Number(LEVEL_Number));
  // Probe on undriven
  or or_4 (or_4_out, d_ff_23_q, d_ff_24_q, d_ff_25_q, d_ff_26_q);
  D_Flip_Flop #(.trigger("high")) d_ff_11 (.clk(CLK), .D(and_6_out), .Q(d_ff_11_q));  // open: Qn, preset, en, reset
  D_Flip_Flop #(.trigger("high")) d_ff_12 (.clk(CLK), .D(and_7_out), .Q(INT_L1_0));  // open: Qn, preset, en, reset
  D_Flip_Flop #(.trigger("high")) d_ff_13 (.clk(CLK), .D(and_8_out), .Q(INT_L1_1));  // open: Qn, preset, en, reset
  D_Flip_Flop #(.trigger("high")) d_ff_14 (.clk(CLK), .D(and_9_out), .Q(INT_L1_2));  // open: Qn, preset, en, reset
  D_Flip_Flop #(.trigger("high")) d_ff_15 (.clk(CLK), .D(and_10_out), .Q(INT_L1_3));  // open: Qn, preset, en, reset
  and and_6 (and_6_out, POWER_FAILURES, d_ff_28_q);
  and and_7 (and_7_out, DISK_0, d_ff_35_q);
  and and_8 (and_8_out, DISK_1, d_ff_33_q);
  and and_9 (and_9_out, DISK_2, d_ff_30_q);
  and and_10 (and_10_out, DISK_3, d_ff_16_q);
  D_Flip_Flop #(.trigger("high")) d_ff_16 (.clk(CLK), .D(1'b1), .Q(d_ff_16_q));  // open: Qn, preset, en, reset
  D_Flip_Flop #(.trigger("high")) d_ff_17 (.clk(CLK), .D(and_11_out), .Q(d_ff_17_q));  // open: Qn, preset, en, reset
  and and_11 (and_11_out, ALARM[0], d_ff_40_q);
  D_Flip_Flop #(.trigger("high")) d_ff_18 (.clk(CLK), .D(and_12_out), .Q(d_ff_18_q));  // open: Qn, preset, en, reset
  and and_12 (and_12_out, ALARM[1], d_ff_39_q);
  D_Flip_Flop #(.trigger("high")) d_ff_19 (.clk(CLK), .D(and_13_out), .Q(d_ff_19_q));  // open: Qn, preset, en, reset
  and and_13 (and_13_out, ALARM[2], d_ff_37_q);
  D_Flip_Flop #(.trigger("high")) d_ff_20 (.clk(CLK), .D(and_14_out), .Q(d_ff_20_q));  // open: Qn, preset, en, reset
  and and_14 (and_14_out, ALARM[3], d_ff_36_q);
  D_Flip_Flop #(.trigger("high")) d_ff_21 (.clk(CLK), .D(and_15_out), .Q(d_ff_21_q));  // open: Qn, preset, en, reset
  and and_15 (and_15_out, ALARM[4], d_ff_31_q);
  D_Flip_Flop #(.trigger("high")) d_ff_22 (.clk(CLK), .D(and_16_out), .Q(d_ff_22_q));  // open: Qn, preset, en, reset
  and and_16 (and_16_out, ALARM[5], d_ff_29_q);
  D_Flip_Flop #(.trigger("high")) d_ff_23 (.clk(CLK), .D(and_17_out), .Q(d_ff_23_q));  // open: Qn, preset, en, reset
  and and_17 (and_17_out, RES[0], d_ff_38_q);
  D_Flip_Flop #(.trigger("high")) d_ff_24 (.clk(CLK), .D(and_18_out), .Q(d_ff_24_q));  // open: Qn, preset, en, reset
  and and_18 (and_18_out, RES[1], d_ff_34_q);
  D_Flip_Flop #(.trigger("high")) d_ff_25 (.clk(CLK), .D(and_19_out), .Q(d_ff_25_q));  // open: Qn, preset, en, reset
  and and_19 (and_19_out, RES[2], d_ff_32_q);
  D_Flip_Flop #(.trigger("high")) d_ff_26 (.clk(CLK), .D(and_20_out), .Q(d_ff_26_q));  // open: Qn, preset, en, reset
  and and_20 (and_20_out, RES[3], d_ff_27_q);
  D_Flip_Flop #(.trigger("high")) d_ff_27 (.clk(CLK), .D(1'b1), .Q(d_ff_27_q));  // open: Qn, preset, en, reset
  D_Flip_Flop #(.trigger("high")) d_ff_28 (.clk(CLK), .D(1'b1), .Q(d_ff_28_q));  // open: Qn, preset, en, reset
  D_Flip_Flop #(.trigger("high")) d_ff_29 (.clk(CLK), .D(1'b0), .Q(d_ff_29_q));  // open: Qn, preset, en, reset
  D_Flip_Flop #(.trigger("high")) d_ff_30 (.clk(CLK), .D(1'b1), .Q(d_ff_30_q));  // open: Qn, preset, en, reset
  D_Flip_Flop #(.trigger("high")) d_ff_31 (.clk(CLK), .D(1'b0), .Q(d_ff_31_q));  // open: Qn, preset, en, reset
  D_Flip_Flop #(.trigger("high")) d_ff_32 (.clk(CLK), .D(1'b1), .Q(d_ff_32_q));  // open: Qn, preset, en, reset
  D_Flip_Flop #(.trigger("high")) d_ff_33 (.clk(CLK), .D(1'b1), .Q(d_ff_33_q));  // open: Qn, preset, en, reset
  D_Flip_Flop #(.trigger("falling")) d_ff_34 (.clk(CLK), .D(1'b1), .Q(d_ff_34_q));  // open: Qn, preset, en, reset
  D_Flip_Flop #(.trigger("high")) d_ff_35 (.clk(CLK), .D(1'b1), .Q(d_ff_35_q));  // open: Qn, preset, en, reset
  D_Flip_Flop #(.trigger("high")) d_ff_36 (.clk(CLK), .D(1'b1), .Q(d_ff_36_q));  // open: Qn, preset, en, reset
  D_Flip_Flop #(.trigger("high")) d_ff_37 (.clk(CLK), .D(1'b1), .Q(d_ff_37_q));  // open: Qn, preset, en, reset
  D_Flip_Flop #(.trigger("falling")) d_ff_38 (.clk(CLK), .D(1'b1), .Q(d_ff_38_q));  // open: Qn, preset, en, reset
  D_Flip_Flop #(.trigger("high")) d_ff_39 (.clk(CLK), .D(1'b1), .Q(d_ff_39_q));  // open: Qn, preset, en, reset
  D_Flip_Flop #(.trigger("high")) d_ff_40 (.clk(CLK), .D(1'b1), .Q(d_ff_40_q));  // open: Qn, preset, en, reset

  // Other names for the same wires on the sheet: ALARM_0 = ALARM[0]; ALARM_1 = ALARM[1]; ALARM_2 = ALARM[2];
  //   ALARM_3 = ALARM[3]; ALARM_4 = ALARM[4]; ALARM_5 = ALARM[5]; Power_Failure = POWER_FAILURES; RES_0 = RES[0];
  //   RES_1 = RES[1]; RES_2 = RES[2]; RES_3 = RES[3]

  // Notes on the sheet:
  //   PART A :
  //   Question 1:
  //   Extensions
  //   VF
  //   CONTROL :
  //   Mask Register
  //   Question 2:
  //   0 since it's additional
  //   0 since it's additional
endmodule

module DAISY_CHAIN_SYSTEM (
  input  INT_REQ_IN0,
  input  INT_REQ_IN1,
  input  INT_REQ_IN2,
  input  INT_REQ_IN3,
  output INT_REQ_OUTPUT,
  output ACK_OUTPUT,
  output [1:0] _2_bit_Device_Number
);

  wire ACK_INPUT_q, and_1_out, and_2_out, and_3_out, and_4_out, clock_1_out, controlled_buffer_1_out,
       daisy_chain_cell_1_interrupt_request_output, daisy_chain_cell_1_output_acknowledgment,
       daisy_chain_cell_2_interrupt_request_output, daisy_chain_cell_2_output_acknowledgment,
       daisy_chain_cell_3_interrupt_request_output, daisy_chain_cell_3_output_acknowledgment,
       daisy_chain_cell_4_interrupt_request_output;

  Clock clock_1 (.out(clock_1_out));
  or or_1 (INT_REQ_OUTPUT, daisy_chain_cell_4_interrupt_request_output, daisy_chain_cell_3_interrupt_request_output, daisy_chain_cell_2_interrupt_request_output, daisy_chain_cell_1_interrupt_request_output);
  D_Flip_Flop #(.trigger("high")) ACK_INPUT (
    .clk(clock_1_out), .D(controlled_buffer_1_out), .Q(ACK_INPUT_q));  // open: Qn, preset, en, reset
  assign controlled_buffer_1_out = INT_REQ_OUTPUT ? 1'b1 : 1'bz;  // Controlled_Buffer controlled_buffer_1
  DAISY_CHAIN_CELL daisy_chain_cell_1 (
    .INTERRUPT_REQUEST_0(INT_REQ_IN0), .INPUT_ACKNOWLEDGMENT(ACK_INPUT_q),
    .Interrupt_request_output(daisy_chain_cell_1_interrupt_request_output),
    .Output_acknowledgment(daisy_chain_cell_1_output_acknowledgment));
  and and_1 (and_1_out, ACK_INPUT_q, INT_REQ_IN0);
  and and_2 (and_2_out, daisy_chain_cell_1_output_acknowledgment, INT_REQ_IN1);
  DAISY_CHAIN_CELL daisy_chain_cell_2 (
    .INTERRUPT_REQUEST_0(INT_REQ_IN1), .INPUT_ACKNOWLEDGMENT(daisy_chain_cell_1_output_acknowledgment),
    .Interrupt_request_output(daisy_chain_cell_2_interrupt_request_output),
    .Output_acknowledgment(daisy_chain_cell_2_output_acknowledgment));
  DAISY_CHAIN_CELL daisy_chain_cell_3 (
    .INTERRUPT_REQUEST_0(INT_REQ_IN2), .INPUT_ACKNOWLEDGMENT(daisy_chain_cell_2_output_acknowledgment),
    .Interrupt_request_output(daisy_chain_cell_3_interrupt_request_output),
    .Output_acknowledgment(daisy_chain_cell_3_output_acknowledgment));
  and and_3 (and_3_out, daisy_chain_cell_2_output_acknowledgment, INT_REQ_IN2);
  and and_4 (and_4_out, daisy_chain_cell_3_output_acknowledgment, INT_REQ_IN3);
  PRIORITY_ENCODER priority_encoder_1 (
    .L0(and_1_out), .L1(and_2_out), .L2(and_3_out), .L3(and_4_out), .Device_Number(_2_bit_Device_Number));
  DAISY_CHAIN_CELL daisy_chain_cell_4 (
    .INTERRUPT_REQUEST_0(INT_REQ_IN3), .INPUT_ACKNOWLEDGMENT(daisy_chain_cell_3_output_acknowledgment),
    .Interrupt_request_output(daisy_chain_cell_4_interrupt_request_output), .Output_acknowledgment(ACK_OUTPUT));

  // Notes on the sheet:
  //   DAISY CHAIN SYSTEM
  //   PART B :
  //   Question 1:
endmodule

module DAISY_CHAIN (
  input  _0C,
  input  _1C0,
  input  _1C1,
  input  _1C2,
  input  _1C3,
  input  [5:0] LEVEL2,
  input  [3:0] LEVEL3,
  output LEVEL_IS_1,
  output [1:0] _2_bit_Cause_Number
);

  wire and_1_out, and_2_out, and_3_out, and_5_out, daisy_chain_cell_1_output_acknowledgment,
       daisy_chain_cell_2_output_acknowledgment, daisy_chain_cell_3_output_acknowledgment,
       daisy_chain_cell_4_output_acknowledgment, interrupt_hierarchy_1_int_l1_0,
       interrupt_hierarchy_1_int_l1_1, interrupt_hierarchy_1_int_l1_2, interrupt_hierarchy_1_int_l1_3,
       not_1_out, or_1_out;
  wire [1:0] interrupt_hierarchy_1_level_number;

  INTERRUPT_HIERARCHY interrupt_hierarchy_1 (
    .POWER_FAILURES(_0C), .DISK_0(_1C0), .DISK_1(_1C1), .DISK_2(_1C2), .DISK_3(_1C3), .ALARM(LEVEL2),
    .RES(LEVEL3), .INT_L1_0(interrupt_hierarchy_1_int_l1_0), .INT_L1_1(interrupt_hierarchy_1_int_l1_1),
    .INT_L1_2(interrupt_hierarchy_1_int_l1_2), .INT_L1_3(interrupt_hierarchy_1_int_l1_3),
    .LEVEL_Number(interrupt_hierarchy_1_level_number));
  DAISY_CHAIN_CELL daisy_chain_cell_1 (
    .INTERRUPT_REQUEST_0(interrupt_hierarchy_1_int_l1_0), .INPUT_ACKNOWLEDGMENT(LEVEL_IS_1),
    .Output_acknowledgment(daisy_chain_cell_1_output_acknowledgment));  // open: Interrupt_request_output
  and and_1 (and_1_out, LEVEL_IS_1, interrupt_hierarchy_1_int_l1_0);
  // Probe on interrupt_hierarchy_1_level_number
  and and_2 (and_2_out, daisy_chain_cell_1_output_acknowledgment, interrupt_hierarchy_1_int_l1_1);
  not not_1 (not_1_out, _0C);
  or or_1 (or_1_out, interrupt_hierarchy_1_int_l1_0, interrupt_hierarchy_1_int_l1_1, interrupt_hierarchy_1_int_l1_2, interrupt_hierarchy_1_int_l1_3);
  DAISY_CHAIN_CELL daisy_chain_cell_2 (
    .INTERRUPT_REQUEST_0(interrupt_hierarchy_1_int_l1_1),
    .INPUT_ACKNOWLEDGMENT(daisy_chain_cell_1_output_acknowledgment),
    .Output_acknowledgment(daisy_chain_cell_2_output_acknowledgment));  // open: Interrupt_request_output
  and and_3 (and_3_out, daisy_chain_cell_2_output_acknowledgment, interrupt_hierarchy_1_int_l1_2);
  and and_4 (LEVEL_IS_1, not_1_out, or_1_out);
  DAISY_CHAIN_CELL daisy_chain_cell_3 (
    .INTERRUPT_REQUEST_0(interrupt_hierarchy_1_int_l1_2),
    .INPUT_ACKNOWLEDGMENT(daisy_chain_cell_2_output_acknowledgment),
    .Output_acknowledgment(daisy_chain_cell_3_output_acknowledgment));  // open: Interrupt_request_output
  DAISY_CHAIN_CELL daisy_chain_cell_4 (
    .INTERRUPT_REQUEST_0(interrupt_hierarchy_1_int_l1_3),
    .INPUT_ACKNOWLEDGMENT(daisy_chain_cell_3_output_acknowledgment),
    .Output_acknowledgment(daisy_chain_cell_4_output_acknowledgment));  // open: Interrupt_request_output
  and and_5 (and_5_out, daisy_chain_cell_3_output_acknowledgment, interrupt_hierarchy_1_int_l1_3);
  PRIORITY_ENCODER priority_encoder_1 (
    .L0(and_1_out), .L1(and_2_out), .L2(and_3_out), .L3(and_5_out), .Device_Number(_2_bit_Cause_Number));
  // Probe on daisy_chain_cell_4_output_acknowledgment

  // Other names for the same wires on the sheet: ACK_IN = LEVEL_IS_1

  // Notes on the sheet:
  //   PART B :
  //   Question 2:
  //   DAISY CHAIN CONFIG
  //   DAISY CHAIN CONFIG
  //   DATA BUS
endmodule

module PRIORITY_ENCODER (
  input  L0,
  input  L1,
  input  L2,
  input  L3,
  output [1:0] Device_Number
);

  wire and_1_out, not_1_out, or_3_out;
  wire [1:0] or_1_out;

  or or_1 (or_1_out[0], and_1_out, L0);
  and and_1 (and_1_out, not_1_out, L2);
  not not_1 (not_1_out, L1);
  or or_2 (or_1_out[1], L1, L0);
  assign Device_Number = or_3_out ? ~or_1_out : 2'bz;  // Controlled_Inverter controlled_inverter_1
  or or_3 (or_3_out, L0, L1, L2, L3);
  // Probe on or_3_out

  // Notes on the sheet:
  //   PRIORITY ENCODER
endmodule

module DAISY_CHAIN_CELL (
  input  INTERRUPT_REQUEST_0,
  input  INPUT_ACKNOWLEDGMENT,
  output Interrupt_request_output,
  output Output_acknowledgment
);

  wire CLK, d_ff_1_qn;

  Clock clock_1 (.out(CLK));
  D_Flip_Flop #(.trigger("high")) d_ff_1 (
    .clk(CLK), .D(INTERRUPT_REQUEST_0), .Q(Interrupt_request_output), .Qn(d_ff_1_qn));  // open: preset, en, reset
  and and_1 (Output_acknowledgment, d_ff_1_qn, INPUT_ACKNOWLEDGMENT);

  // Notes on the sheet:
  //   DAISY CHAIN CELL
endmodule

module THE_PHASE_DISTRIBUTOR (
  input  CONTROL_DISTRIBUTOR,
  output \Θ0 ,
  output \Θ1 ,
  output \Θ2 ,
  output \Θ3 ,
  output \Φ0 ,
  output \Φ1 ,
  output \Φ2 ,
  output \Φ3 
);

  wire and_1_out, clock_1_out, not_1_out;
  wire [1:0] counter_1_q;

  Clock clock_1 (.out(clock_1_out));
  not not_1 (not_1_out, CONTROL_DISTRIBUTOR);
  and and_1 (and_1_out, clock_1_out, CONTROL_DISTRIBUTOR);
  Counter #(.width(2), .max('h3), .trigger("falling")) counter_1 (
    .Q(counter_1_q), .clk(and_1_out), .clr(not_1_out));  // open: load, D, count, carry
  Decoder #(.select(2)) decoder_1 (.out0(\Φ0 ), .out1(\Φ1 ), .out2(\Φ2 ), .out3(\Φ3 ), .sel(counter_1_q));  // open: en
  and and_2 (\Θ0 , and_1_out, \Φ0 );
  and and_3 (\Θ1 , and_1_out, \Φ1 );
  and and_4 (\Θ2 , and_1_out, \Φ2 );
  and and_5 (\Θ3 , and_1_out, \Φ3 );

  // Notes on the sheet:
  //   PART C :
  //   Question 1:
endmodule

module ROM (
  input  [1:0] CAUSE_NUMBER,
  input  READ,
  output [7:0] MEMORY_ADDRESS
);

  wire CLOCK_out, decoder_1_out0, decoder_1_out1, decoder_1_out2, decoder_1_out3, pull_resistor_1_node,
       pull_resistor_3_node, pull_resistor_5_node, pull_resistor_7_node, transistor_1_out, transistor_3_out,
       transistor_7_out, transistor_12_out;

  Decoder #(.select(2)) decoder_1 (
    .out0(decoder_1_out0), .out1(decoder_1_out1), .out2(decoder_1_out2), .out3(decoder_1_out3),
    .sel(CAUSE_NUMBER));  // open: en
  Pull_Resistor pull_resistor_1 (.node(pull_resistor_1_node));
  Clock CLOCK (.out(CLOCK_out));
  Transistor #(.\type ("n")) transistor_1 (.in(1'b1), .out(transistor_1_out), .gate(decoder_1_out3));
  Register #(.width(1), .trigger("high")) register_1 (
    .D(pull_resistor_1_node), .en(READ), .Q(MEMORY_ADDRESS[7]), .clk(CLOCK_out));  // open: clr
  Pull_Resistor pull_resistor_2 (.node(transistor_1_out));
  Register #(.width(1), .trigger("high")) register_2 (
    .D(transistor_1_out), .en(READ), .Q(MEMORY_ADDRESS[6]), .clk(CLOCK_out));  // open: clr
  Pull_Resistor pull_resistor_3 (.node(pull_resistor_3_node));
  Transistor #(.\type ("n")) transistor_2 (.in(1'b1), .out(pull_resistor_3_node), .gate(decoder_1_out2));
  Transistor #(.\type ("n")) transistor_3 (.in(1'b1), .out(transistor_3_out), .gate(decoder_1_out1));
  Transistor #(.\type ("n")) transistor_4 (.in(1'b1), .out(transistor_3_out), .gate(decoder_1_out2));
  Register #(.width(1), .trigger("high")) register_3 (
    .D(pull_resistor_3_node), .en(READ), .Q(MEMORY_ADDRESS[5]), .clk(CLOCK_out));  // open: clr
  Pull_Resistor pull_resistor_4 (.node(transistor_3_out));
  Register #(.width(1), .trigger("high")) register_4 (
    .D(transistor_3_out), .en(READ), .Q(MEMORY_ADDRESS[4]), .clk(CLOCK_out));  // open: clr
  Pull_Resistor pull_resistor_5 (.node(pull_resistor_5_node));
  Transistor #(.\type ("n")) transistor_5 (.in(1'b1), .out(pull_resistor_5_node), .gate(decoder_1_out0));
  Transistor #(.\type ("n")) transistor_6 (.in(1'b1), .out(pull_resistor_5_node), .gate(decoder_1_out1));
  Transistor #(.\type ("n")) transistor_7 (.in(1'b1), .out(transistor_7_out), .gate(decoder_1_out0));
  Transistor #(.\type ("n")) transistor_8 (.in(1'b1), .out(transistor_7_out), .gate(decoder_1_out1));
  Transistor #(.\type ("n")) transistor_9 (.in(1'b1), .out(transistor_7_out), .gate(decoder_1_out3));
  Register #(.width(1), .trigger("high")) register_5 (
    .D(pull_resistor_5_node), .en(READ), .Q(MEMORY_ADDRESS[3]), .clk(CLOCK_out));  // open: clr
  Pull_Resistor pull_resistor_6 (.node(transistor_7_out));
  Register #(.width(1), .trigger("high")) register_6 (
    .D(transistor_7_out), .en(READ), .Q(MEMORY_ADDRESS[2]), .clk(CLOCK_out));  // open: clr
  Pull_Resistor pull_resistor_7 (.node(pull_resistor_7_node));
  Transistor #(.\type ("n")) transistor_10 (.in(1'b1), .out(pull_resistor_7_node), .gate(decoder_1_out0));
  Transistor #(.\type ("n")) transistor_11 (.in(1'b1), .out(pull_resistor_7_node), .gate(decoder_1_out3));
  Transistor #(.\type ("n")) transistor_12 (.in(1'b1), .out(transistor_12_out), .gate(decoder_1_out0));
  Register #(.width(1), .trigger("high")) register_7 (
    .D(pull_resistor_7_node), .en(READ), .Q(MEMORY_ADDRESS[1]), .clk(CLOCK_out));  // open: clr
  Pull_Resistor pull_resistor_8 (.node(transistor_12_out));
  Register #(.width(1), .trigger("high")) register_8 (
    .D(transistor_12_out), .en(READ), .Q(MEMORY_ADDRESS[0]), .clk(CLOCK_out));  // open: clr

  // Other names for the same wires on the sheet: tunnel[7:0] = MEMORY_ADDRESS

  // Notes on the sheet:
  //   PART C :
  //   Question 2:
endmodule

module SEQUENCER (
  input  CONTROL,
  input  [1:0] IT_NUMBER,
  output [7:0] PC_CONTENT,
  output S0,
  output S1,
  output S2,
  output S3,
  output [7:0] DATA_BUS_CONTENT
);

  wire not_1_out, \Θ0 , \Θ1 , \Θ2 , \Θ3 ;
  wire [1:0] RAR_q;
  wire [7:0] bit_extender_1_out, IPC_out, rom_1_memory_address, TDA_out;

  not not_1 (not_1_out, CONTROL);
  THE_PHASE_DISTRIBUTOR the_phase_distributor_1 (
    .CONTROL_DISTRIBUTOR(CONTROL), .\Θ0 (\Θ0 ), .\Φ0 (S0), .\Θ1 (\Θ1 ), .\Φ1 (S1), .\Θ2 (\Θ2 ), .\Φ2 (S2),
    .\Θ3 (\Θ3 ), .\Φ3 (S3));
  assign bit_extender_1_out = {{6{1'b0}}, IT_NUMBER};  // Bit_Extender bit_extender_1
  Register #(.width(2), .trigger("high")) RAR (.D(IT_NUMBER), .Q(RAR_q), .clk(\Θ1 ));  // open: en, clr
  assign DATA_BUS_CONTENT = S1 ? bit_extender_1_out : 8'bz;  // Controlled_Buffer controlled_buffer_1
  ROM rom_1 (.CAUSE_NUMBER(RAR_q), .READ(S2), .MEMORY_ADDRESS(rom_1_memory_address));
  assign DATA_BUS_CONTENT = S3 ? rom_1_memory_address : 8'bz;  // Controlled_Buffer OROM
  assign TDA_out = S3 ? DATA_BUS_CONTENT : 8'bz;  // Controlled_Buffer TDA
  Register #(.trigger("high")) PC (.D(IPC_out), .Q(PC_CONTENT), .clk(\Θ3 ), .clr(not_1_out));  // open: en
  assign IPC_out = \Θ3  ? TDA_out : 8'bz;  // Controlled_Buffer IPC

  // Other names for the same wires on the sheet: Φ0 = S0; Φ1 = S1; Φ2 = S2; Φ3 = S3

  // Notes on the sheet:
  //   PART C :
  //   Question 3:
  //   DATA BUS
  //   R
endmodule

module DRAW (
  input  CLK,
  input  \Φ0 ,
  input  \Θ0 ,
  input  \Φ1 ,
  input  \Θ1 ,
  input  \Φ2 ,
  input  \Θ2 ,
  input  \Φ3 ,
  input  \Θ3 ,
  input  INTERRUPT_LEVEL,
  input  INTERRUPT_CAUSE,
  input  IRAR,
  input  R,
  input  OROM,
  input  TDA,
  input  IPC,
  input  PC
);


  // Notes on the sheet:
  //   PART C :
  //   QUESTION 4:
endmodule

module MAIN (
  input  _0C,
  input  _1C0,
  input  _1C1,
  input  _1C2,
  input  [5:0] _2C,
  input  _1C3,
  input  [3:0] _3C,
  output [7:0] PC,
  output [7:0] DATA_BUS
);

  wire daisy_chain_1_level_is_1, interrupt_hierarchy_1_int_l1_0, interrupt_hierarchy_1_int_l1_1,
       interrupt_hierarchy_1_int_l1_2, interrupt_hierarchy_1_int_l1_3, sequencer_1_s0, sequencer_1_s1,
       sequencer_1_s2, sequencer_1_s3;
  wire [1:0] daisy_chain_1__2_bit_cause_number, interrupt_hierarchy_1_level_number;

  INTERRUPT_HIERARCHY interrupt_hierarchy_1 (
    .POWER_FAILURES(_0C), .DISK_0(_1C0), .DISK_1(_1C1), .DISK_2(_1C2), .DISK_3(_1C3), .ALARM(_2C), .RES(_3C),
    .INT_L1_0(interrupt_hierarchy_1_int_l1_0), .INT_L1_1(interrupt_hierarchy_1_int_l1_1),
    .INT_L1_2(interrupt_hierarchy_1_int_l1_2), .INT_L1_3(interrupt_hierarchy_1_int_l1_3),
    .LEVEL_Number(interrupt_hierarchy_1_level_number));
  // Probe on interrupt_hierarchy_1_level_number
  DAISY_CHAIN daisy_chain_1 (
    ._0C(_0C), ._1C0(interrupt_hierarchy_1_int_l1_0), ._1C1(interrupt_hierarchy_1_int_l1_1),
    ._1C2(interrupt_hierarchy_1_int_l1_2), ._1C3(interrupt_hierarchy_1_int_l1_3), .LEVEL2(_2C), .LEVEL3(_3C),
    .LEVEL_IS_1(daisy_chain_1_level_is_1), ._2_bit_Cause_Number(daisy_chain_1__2_bit_cause_number));
  SEQUENCER sequencer_1 (
    .IT_NUMBER(daisy_chain_1__2_bit_cause_number), .PC_CONTENT(PC), .DATA_BUS_CONTENT(DATA_BUS),
    .S0(sequencer_1_s0), .S1(sequencer_1_s1), .S2(sequencer_1_s2), .S3(sequencer_1_s3),
    .CONTROL(daisy_chain_1_level_is_1));
  LED STEP0 (.in(sequencer_1_s0));
  LED STEP1 (.in(sequencer_1_s1));
  LED STEP2 (.in(sequencer_1_s2));
  LED STEP3 (.in(sequencer_1_s3));

  // Notes on the sheet:
  //   PART C :
  //   Question 5:
  //   ALL SYSTEM COMPONENTS
endmodule
